// Digital circuit RV5-PROCESSOR.dig as structural Verilog
module RV5_PROCESSOR (
  input  in_1,
  input  in_2,
  input  clock,
  input  in_4,
  input  in_5
);

  wire abstractauto_wen, abstractcs_busy, abstractcs_wen, ack_drop, and_5_out, and_8_out, and_9_out,
       and_11_out, and_12_out, and_13_out, and_14_out, and_15_out, and_16_out, and_17_out, and_18_out,
       and_19_out, and_21_out, and_22_out, and_27_out, and_34_out, and_37_out, and_39_out, autoexec, br_cond,
       branch_sel, command_exec, command_reg_aarpostincrement, command_reg_arg0wen, command_reg_exec,
       command_reg_jumpprogbuf, command_reg_postexec, command_reg_regnoinvalid, command_reg_regwen,
       command_reg_sel, command_reg_transfer, command_reg_validtransferex, command_reg_write,
       command_unsuported_sel, command_wen, comparator_1_eq, comparator_2_eq, comparator_3_eq,
       comparator_4_eq, comparator_5_eq, comparator_6_eq, comparator_7_eq, comparator_8_eq, comparator_9_eq,
       comparator_11_eq, comparator_12_eq, comparator_14_gt, comparator_15_lt, comparator_16_gt,
       comparator_18_lt, comparator_19_gt, comparator_20_eq, comparator_21_eq, comparator_22_eq,
       comparator_23_eq, comparator_24_eq, comparator_25_eq, csr_opclear, csr_opset, csr_useimm, csr_wen,
       d_ff_1_q, d_ff_2_q, d_ff_3_q, d_ff_4_q, d_ff_6_nq, d_ff_7_q, d_ff_8_q, d_memwen, d_memwen_t, d_regwen,
       d_regwen_t, dm_ack, dm_done, dm_wen, dmcontrol_ackhavereset, dmcontrol_clrresethaltreq,
       dmcontrol_dmactive, dmcontrol_haltreq, dmcontrol_hartreset, dmcontrol_hasel, dmcontrol_ndmreset,
       dmcontrol_wen, dmi_access, dmi_ren, dmi_req, dmi_req_rise, dmi_wen, dmstatus_allhalted,
       dmstatus_allnonexistent, dmstatus_allresumeack, dmstatus_allrunning, DPC194, dret_sel, ebreak_sel,
       ecall_sel, gdbserver_1_p1, gdbserver_1_p3, gdbserver_1_p4, gdbserver_1_p5, haltreq, IF_jalr_sel,
       IF_mret_sel, jal_sel, multiplexer_17_out, nor_1_out, nor_2_out, not_1_out, not_2_out, not_4_out,
       not_5_out, not_7_out, not_9_out, not_10_out, not_11_out, not_12_out, not_13_out, not_14_out,
       not_15_out, or_1_out, or_2_out, or_3_out, or_6_out, or_7_out, or_9_out, or_10_out, or_12_out,
       or_14_out, or_15_out, or_16_out, or_17_out, register_3_q, rs_ff_as_1_q, rv5_control_1_alu_bsel,
       rv5_control_1_alu_mod, rv5_control_1_ld_signext, rv5_control_1_ram_b, rv5_control_1_ram_h,
       rv5_control_1_ram_ren, rv5_tap_1_dmi_req, rv5_tap_1_dmi_write, sbcs_wen, stopcond;
  wire [1:0] rv5_control_1_alu_asel, rv5_control_1_wb_sel, rv5_imm_gen_1_p3;
  wire [2:0] abstractcs_cmderr, and_24_out, command_reg_aarsize, dmi_rdata_lut_out, dmi_wen_lut_out,
       multiplexer_8_out, multiplexer_9_out, not_6_out, rv5_control_1_alu_op, rv5_control_1_imm_sel;
  wire [4:0] command_reg_gprno, d_rd, d_rd_t, d_rs1, d_rs1_t;
  wire [6:0] rv5_tap_1_dmi_addr;
  wire [7:0] command_cmdtype;
  wire [11:0] abstractauto_autoexecdata;
  wire [15:0] abstractauto_autoexecprogbuf, command_reg_regno;
  wire [15:5] sub_1_s;
  wire [15:12] abstractauto_persistent;
  wire [19:0] dmcontrol_hartsel;
  wire [23:23] multiplexer_15_out;
  wire [29:0] IF_pc_jumprel, PC_Incr_s, rv5_imm_gen_1_p3_2, rv5_pc_select_1_pc;
  wire [30:2] dmcontrol_persistent;
  wire [30:3] dmcontrol_rdata;
  wire [31:0] addr_dm, alu_out, and_26_out, command_persistent_q, csr_out, d_rdin, d_rdin_t, dcsr, dm_wdata,
       dmi_memaddr, dmi_rdata, dmi_wdata, dpc, IF_mepc, IF_mtvec, inst_out, multiplexer_1_out,
       multiplexer_10_out, multiplexer_11_out, multiplexer_12_out, multiplexer_13_out, multiplexer_14_out,
       not_8_out, or_11_out, out_dm, ra, rv5_gpr_1_rb, rv5_memory_1_p13;
  wire [31:2] add_1_s, ID_pc;

  // GdbServer gdbserver_1: pin names not known; wires that end beside it: gdbserver_1_p1, clock, gdbserver_1_p3, gdbserver_1_p4, gdbserver_1_p5
  RV5_TAP rv5_tap_1 (
    .TCK(gdbserver_1_p3), .TMS(gdbserver_1_p4), .TDI(gdbserver_1_p5), .DMI_ACK(dm_ack),
    .DMI_RDATA(dmi_rdata), .DMI_STATUS({2{abstractcs_busy}}), .TDO(gdbserver_1_p1),
    .DMI_REQ(rv5_tap_1_dmi_req), .DMI_WDATA(dmi_wdata), .DMI_ADDR(rv5_tap_1_dmi_addr),
    .DMI_WRITE(rv5_tap_1_dmi_write));
  Register #(.Bits(32)) u_dmcontrol_persistent (
    .D(dmi_wdata), .C(clock), .en(dmcontrol_wen),
    .Q({dmcontrol_haltreq, dmcontrol_persistent[30], dmcontrol_hartreset, dmcontrol_persistent[28:27], dmcontrol_hasel, dmcontrol_hartsel[9:0], dmcontrol_hartsel[19:10], dmcontrol_persistent[5:2], dmcontrol_ndmreset, dmcontrol_dmactive}));
  and and_1 (dmcontrol_clrresethaltreq, dmcontrol_wen, dmi_wdata[2]);
  and and_2 (dmcontrol_rdata[3], dmcontrol_wen, dmi_wdata[3]);
  and and_3 (dmcontrol_ackhavereset, dmcontrol_wen, dmi_wdata[28]);
  and and_4 (dmcontrol_rdata[30], dmcontrol_wen, dmi_wdata[30]);
  and and_5 (and_5_out, dmcontrol_rdata[30], dcsr[2]);
  D_FF d_ff_1 (.D(and_5_out), .C(clock), .Q(d_ff_1_q));  // open: nQ
  D_FF d_ff_2 (.D(d_ff_1_q), .C(clock), .Q(d_ff_2_q));  // open: nQ
  D_FF d_ff_3 (.D(d_ff_2_q), .C(clock), .Q(d_ff_3_q));  // open: nQ
  D_FF d_ff_4 (.D(rv5_tap_1_dmi_req), .C(clock), .Q(d_ff_4_q));  // open: nQ
  D_FF d_ff_5 (.D(d_ff_4_q), .C(clock), .Q(dmi_req));  // open: nQ
  and and_6 (dmi_wen, rv5_tap_1_dmi_write, dmi_req_rise);
  and and_7 (dmi_ren, not_1_out, dmi_req_rise);
  not not_1 (not_1_out, rv5_tap_1_dmi_write);
  or or_1 (or_1_out, dmcontrol_haltreq, d_ff_3_q);
  RISING_EDGE rising_edge_1 (.clk(clock), .d(dmi_req), .o(dmi_req_rise));
  and and_8 (and_8_out, or_1_out, not_2_out);
  not not_2 (not_2_out, dmstatus_allhalted);
  RISING_EDGE rising_edge_2 (.clk(clock), .d(and_8_out), .o(haltreq));
  LookUpTable #(.Bits(3)) dmi_rdata_lut (
    .in0(rv5_tap_1_dmi_addr[0]), .in1(rv5_tap_1_dmi_addr[1]), .in2(rv5_tap_1_dmi_addr[2]),
    .in3(rv5_tap_1_dmi_addr[3]), .in4(rv5_tap_1_dmi_addr[4]), .in5(rv5_tap_1_dmi_addr[5]),
    .in6(rv5_tap_1_dmi_addr[6]), .out(dmi_rdata_lut_out));
  LookUpTable #(.Bits(3)) dmi_wen_lut (
    .in0(rv5_tap_1_dmi_addr[0]), .in1(rv5_tap_1_dmi_addr[1]), .in2(rv5_tap_1_dmi_addr[2]),
    .in3(rv5_tap_1_dmi_addr[3]), .in4(rv5_tap_1_dmi_addr[4]), .in5(rv5_tap_1_dmi_addr[5]),
    .in6(rv5_tap_1_dmi_addr[6]), .out(dmi_wen_lut_out));
  LookUpTable #(.Bits(32)) dmi_memaddr_lut (
    .in0(rv5_tap_1_dmi_addr[0]), .in1(rv5_tap_1_dmi_addr[1]), .in2(rv5_tap_1_dmi_addr[2]),
    .in3(rv5_tap_1_dmi_addr[3]), .in4(rv5_tap_1_dmi_addr[4]), .in5(rv5_tap_1_dmi_addr[5]),
    .in6(rv5_tap_1_dmi_addr[6]), .out(dmi_memaddr));
  Multiplexer #(.Selector_Bits(3), .Bits(32)) multiplexer_1 (
    .sel(dmi_rdata_lut_out), .in_0({32{1'b0}}), .in_1(out_dm),
    .in_2({dmcontrol_haltreq, dmcontrol_rdata[30], dmcontrol_hartreset, dmcontrol_ackhavereset, 1'b0, dmcontrol_hasel, dmcontrol_hartsel[9:0], dmcontrol_hartsel[19:10], 2'b00, dmcontrol_rdata[3], dmcontrol_clrresethaltreq, dmcontrol_ndmreset, dmcontrol_dmactive}),
    .in_3({{14{1'b0}}, {2{dmstatus_allresumeack}}, {2{dmstatus_allnonexistent}}, 2'b00, {2{dmstatus_allrunning}}, {2{dmstatus_allhalted}}, 8'h82}),
    .in_4(32'h111ffc), .in_5({19'h4000, abstractcs_busy, 1'b0, abstractcs_cmderr, 8'h1}),
    .in_6(32'h20000000), .in_7({abstractauto_autoexecprogbuf, 4'b0000, abstractauto_autoexecdata}),
    .out(multiplexer_1_out));
  Demultiplexer #(.Selector_Bits(3)) demultiplexer_1 (
    .sel(dmi_wen_lut_out), .in(dmi_wen), .out_1(dmcontrol_wen), .out_2(abstractcs_wen), .out_3(command_wen),
    .out_4(sbcs_wen), .out_5(abstractauto_wen));  // open: out_0, out_6, out_7
  and and_9 (and_9_out, dmi_ren, dmi_req_rise);
  Comparator #(.Bits(32)) comparator_1 (.a(dmi_memaddr), .b(32'hffc), .eq(comparator_1_eq));  // open: gt, lt
  Comparator #(.Bits(32)) comparator_2 (.a(dmi_memaddr), .b(32'h1004), .eq(comparator_2_eq));  // open: gt, lt
  Comparator #(.Bits(32)) comparator_3 (.a(dmi_memaddr), .b(32'h1008), .eq(comparator_3_eq));  // open: gt, lt
  Comparator #(.Bits(32)) comparator_4 (.a(dmi_memaddr), .b(32'h100c), .eq(comparator_4_eq));  // open: gt, lt
  Comparator #(.Bits(32)) comparator_5 (.a(dmi_memaddr), .b(32'h1010), .eq(comparator_5_eq));  // open: gt, lt
  Comparator #(.Bits(32)) comparator_6 (.a(dmi_memaddr), .b(32'h1014), .eq(comparator_6_eq));  // open: gt, lt
  Comparator #(.Bits(32)) comparator_7 (.a(dmi_memaddr), .b(32'h1018), .eq(comparator_7_eq));  // open: gt, lt
  Comparator #(.Bits(32)) comparator_8 (.a(dmi_memaddr), .b(32'h101c), .eq(comparator_8_eq));  // open: gt, lt
  Comparator #(.Bits(32)) comparator_9 (.a(dmi_memaddr), .b(32'h1020), .eq(comparator_9_eq));  // open: gt, lt
  Register #(.Bits(32)) register_1 (.D(multiplexer_1_out), .C(clock), .en(and_9_out), .Q(dmi_rdata));
  or or_2 (or_2_out, dmi_ren, dmi_wen);
  and and_10 (dmi_access, or_2_out, dmi_req_rise);
  and and_11 (and_11_out, comparator_1_eq, dmi_access, abstractauto_autoexecdata[0]);
  and and_12 (and_12_out, comparator_2_eq, dmi_access, abstractauto_autoexecprogbuf[0]);
  and and_13 (and_13_out, comparator_3_eq, dmi_access, abstractauto_autoexecprogbuf[1]);
  and and_14 (and_14_out, comparator_4_eq, dmi_access, abstractauto_autoexecprogbuf[2]);
  and and_15 (and_15_out, comparator_5_eq, dmi_access, abstractauto_autoexecprogbuf[3]);
  and and_16 (and_16_out, comparator_6_eq, dmi_access, abstractauto_autoexecprogbuf[4]);
  and and_17 (and_17_out, comparator_7_eq, dmi_access, abstractauto_autoexecprogbuf[5]);
  and and_18 (and_18_out, comparator_8_eq, dmi_access, abstractauto_autoexecprogbuf[6]);
  and and_19 (and_19_out, comparator_9_eq, dmi_access, abstractauto_autoexecprogbuf[7]);
  not not_3 (dmstatus_allrunning, dmstatus_allhalted);
  Comparator #(.Bits(20)) comparator_10 (
    .a(dmcontrol_hartsel), .b({20{1'b0}}), .gt(dmstatus_allnonexistent));  // open: eq, lt
  RS_FF rs_ff_1 (.S(dmcontrol_rdata[30]), .C(clock), .R(dmcontrol_haltreq), .Q(dmstatus_allresumeack));  // open: nQ
  nor nor_1 (nor_1_out, dmi_req_rise, abstractcs_busy);
  or or_3 (or_3_out, dm_done, ack_drop);
  and and_20 (ack_drop, not_4_out, dm_ack);
  not not_4 (not_4_out, dmi_req);
  or or_4 (autoexec, and_11_out, and_12_out, and_13_out, and_14_out, and_15_out, and_16_out, and_17_out, and_18_out, and_19_out);
  RISING_EDGE rising_edge_3 (.clk(clock), .d(nor_1_out), .o(dm_done));
  Register register_2 (.D(dm_done), .C(clock), .en(or_3_out), .Q(dm_ack));
  Comparator #(.Bits(32)) comparator_11 (.a(dmi_memaddr), .b({32{1'b0}}), .eq(comparator_11_eq));  // open: gt, lt
  not not_5 (not_5_out, comparator_11_eq);
  and and_21 (and_21_out, dmi_wen, not_5_out);
  Multiplexer #(.Bits(32)) multiplexer_2 (.sel(command_reg_arg0wen), .in_0(dmi_wdata), .in_1(ra), .out(dm_wdata));
  or or_5 (dm_wen, and_21_out, command_reg_arg0wen);
  Multiplexer #(.Bits(32)) multiplexer_3 (
    .sel(command_reg_validtransferex), .in_0(dmi_memaddr), .in_1(32'hffc), .out(addr_dm));
  RV5_PC_SELECT rv5_pc_select_1 (
    .pc_plus_4(PC_Incr_s), .pc_jumprel(IF_pc_jumprel), .alu_out(alu_out), .mtvec(IF_mtvec), .mepc(IF_mepc),
    .dpc(dpc), .branch_sel(branch_sel), .br_cond(br_cond), .jal_sel(jal_sel), .jalr_sel(IF_jalr_sel),
    .ecall_sel(ecall_sel), .mret_sel(IF_mret_sel), .is_debug(dmstatus_allhalted), .dcsr(dcsr),
    .dret_sel(dret_sel), .haltreq(haltreq), .command_reg_jumpprogbuf(command_reg_jumpprogbuf),
    .dmcontrol_resumereq(dmcontrol_rdata[30]), .ebreak_sel(ebreak_sel), .clk(clock), .pc(rv5_pc_select_1_pc));
  and and_22 (and_22_out, command_reg_regnoinvalid, command_reg_transfer);
  D_FF #(.Bits(30)) PC_w (.D(rv5_pc_select_1_pc), .C(clock), .Q(ID_pc));  // open: nQ
  Comparator #(.Bits(32)) comparator_12 (.a({ID_pc, 2'b00}), .b(32'h190), .eq(comparator_12_eq));  // open: gt, lt
  Comparator #(.Bits(32)) comparator_13 (.a({ID_pc, 2'b00}), .b(32'h194), .eq(DPC194));  // open: gt, lt
  Comparator #(.Bits(32)) comparator_14 (.a({ID_pc, 2'b00}), .b(32'h1003), .gt(comparator_14_gt));  // open: eq, lt
  Comparator #(.Bits(32)) comparator_15 (.a({ID_pc, 2'b00}), .b(32'h1021), .lt(comparator_15_lt));  // open: gt, eq
  Multiplexer #(.Bits(5)) multiplexer_4 (.sel(command_reg_exec), .in_0(d_rs1), .in_1(command_reg_gprno), .out(d_rs1_t));
  Multiplexer #(.Bits(32)) multiplexer_5 (.sel(command_reg_exec), .in_0(d_rdin), .in_1(out_dm), .out(d_rdin_t));
  Multiplexer #(.Bits(5)) multiplexer_6 (.sel(command_reg_regwen), .in_0(d_rd), .in_1(command_reg_gprno), .out(d_rd_t));
  or or_6 (or_6_out, d_regwen, command_reg_regwen);
  or or_7 (or_7_out, comparator_12_eq, DPC194);
  Add #(.Bits(30)) PC_Incr (.a(ID_pc), .b(30'h1), .c_i(1'b0), .s(PC_Incr_s));  // open: c_o
  and and_23 (abstractcs_busy, comparator_14_gt, comparator_15_lt);
  Comparator #(.Bits(3)) comparator_16 (.a(command_reg_aarsize), .b(3'b010), .gt(comparator_16_gt));  // open: eq, lt
  Multiplexer multiplexer_7 (.sel(haltreq), .in_0(or_6_out), .in_1(1'b0), .out(d_regwen_t));
  or or_8 (dmstatus_allhalted, or_7_out, abstractcs_busy);
  or or_9 (or_9_out, command_unsuported_sel, comparator_16_gt, and_22_out, command_reg_aarpostincrement);
  Multiplexer #(.Bits(3)) multiplexer_8 (.sel(or_9_out), .in_0(3'b000), .in_1(3'b010), .out(multiplexer_8_out));
  assign and_24_out = not_6_out & abstractcs_cmderr;  // And and_24, 3 bits wide
  assign not_6_out = ~dmi_wdata[10:8];  // Not not_6, 3 bits wide
  and and_25 (d_memwen_t, d_memwen, not_7_out);
  not not_7 (not_7_out, haltreq);
  Multiplexer #(.Bits(3)) multiplexer_9 (
    .sel(command_reg_exec), .in_0(and_24_out), .in_1(multiplexer_8_out), .out(multiplexer_9_out));
  Multiplexer #(.Bits(32)) multiplexer_10 (
    .sel(csr_useimm), .in_0(ra), .in_1({{27{1'b0}}, d_rs1}), .out(multiplexer_10_out));
  assign not_8_out = ~multiplexer_10_out;  // Not not_8, 32 bits wide
  or or_10 (or_10_out, abstractcs_wen, command_exec);
  RV5_CONTROL rv5_control_1 (
    .opcode(inst_out[6:0]), .funct3(inst_out[14:12]), .system_imm(inst_out[31:20]),
    .imm_sel(rv5_control_1_imm_sel), .reg_wen(d_regwen), .wb_sel(rv5_control_1_wb_sel), .ram_wen(d_memwen),
    .ram_ren(rv5_control_1_ram_ren), .ram_b(rv5_control_1_ram_b), .ram_h(rv5_control_1_ram_h),
    .ld_signext(rv5_control_1_ld_signext), .alu_asel(rv5_control_1_alu_asel), .alu_op(rv5_control_1_alu_op),
    .alu_bsel(rv5_control_1_alu_bsel), .alu_mod(rv5_control_1_alu_mod), .branch_sel(branch_sel),
    .jal_sel(jal_sel), .jalr_sel(IF_jalr_sel), .csr_wen(csr_wen), .csr_opset(csr_opset),
    .csr_opclear(csr_opclear), .csr_useimm(csr_useimm), .csr_is_ecall(ecall_sel), .csr_is_ebreak(ebreak_sel),
    .csr_is_mret(IF_mret_sel), .csr_is_dret(dret_sel));
  assign and_26_out = not_8_out & csr_out;  // And and_26, 32 bits wide
  assign or_11_out = multiplexer_10_out | csr_out;  // Or or_11, 32 bits wide
  Register #(.Bits(3)) u_abstractcs_cmderr (.D(multiplexer_9_out), .C(clock), .en(or_10_out), .Q(abstractcs_cmderr));
  Multiplexer #(.Bits(32)) multiplexer_11 (
    .sel(csr_opclear), .in_0(multiplexer_10_out), .in_1(and_26_out), .out(multiplexer_11_out));
  // RV5_IMM_GEN rv5_imm_gen_1: pin names not known; wires that end beside it: {inst_out[31:20], d_rs1, inst_out[14:12], d_rd, inst_out[6:0]}, rv5_control_1_imm_sel, {rv5_imm_gen_1_p3_2, rv5_imm_gen_1_p3}
  Multiplexer #(.Bits(32)) multiplexer_12 (
    .sel(csr_opset), .in_0(multiplexer_11_out), .in_1(or_11_out), .out(multiplexer_12_out));
  RV5_CSR rv5_csr_1 (
    .clk(clock), .addr(inst_out[31:20]), .w_data(multiplexer_12_out), .wen(csr_wen), .pc_in({ID_pc, 2'b00}),
    .ecall_sel(ecall_sel), .mret_sel(IF_mret_sel), .ebreak_sel(ebreak_sel), .is_debug(dmstatus_allhalted),
    .haltreq(haltreq), .R_DATA(csr_out), .MTVEC_OUT(IF_mtvec), .MEPC_OUT(IF_mepc), .DCSR_OUT(dcsr),
    .DPC_OUT(dpc));
  RV5_GPR rv5_gpr_1 (
    .RS1(d_rs1_t), .RS2(inst_out[24:20]), .D_in(d_rdin_t), .clk(clock), .RD(d_rd_t), .WEN(d_regwen_t),
    .RA(ra), .RB(rv5_gpr_1_rb));  // open: RD0
  Multiplexer #(.Selector_Bits(2), .Bits(32)) multiplexer_13 (
    .sel(rv5_control_1_alu_asel), .in_0(ra), .in_1({ID_pc, 2'b00}), .in_2({32{1'b0}}), .in_3({32{1'b0}}),
    .out(multiplexer_13_out));
  Multiplexer #(.Bits(32)) multiplexer_14 (
    .sel(rv5_control_1_alu_bsel), .in_0(rv5_gpr_1_rb), .in_1({rv5_imm_gen_1_p3_2, rv5_imm_gen_1_p3}),
    .out(multiplexer_14_out));
  Add #(.Bits(30)) PC_JumpRel (.a(ID_pc), .b(rv5_imm_gen_1_p3_2), .c_i(1'b0), .s(IF_pc_jumprel));  // open: c_o
  // RV5_ALU rv5_alu_1: pin names not known; wires that end beside it: multiplexer_13_out, rv5_control_1_alu_op, multiplexer_14_out, rv5_control_1_alu_mod, alu_out, br_cond
  // RV5_MEMORY rv5_memory_1: pin names not known; wires that end beside it: alu_out, rv5_gpr_1_rb, d_memwen_t, rv5_control_1_ram_ren, clock, rv5_control_1_ram_b, rv5_control_1_ram_h, rv5_control_1_ld_signext, {ID_pc, 2'b00}, addr_dm, dm_wen, dm_wdata, rv5_memory_1_p13, {inst_out[31:20], d_rs1, inst_out[14:12], d_rd, inst_out[6:0]}, out_dm
  Register #(.Bits(32)) command_persistent (.D(dmi_wdata), .C(clock), .en(command_wen), .Q(command_persistent_q));
  D_FF d_ff_6 (.D(command_wen), .C(clock), .nQ(d_ff_6_nq));  // open: Q
  and and_27 (and_27_out, d_ff_6_nq, command_wen);
  nor nor_2 (nor_2_out, abstractcs_cmderr[0], abstractcs_cmderr[1], abstractcs_cmderr[2]);
  Comparator #(.Bits(8)) comparator_17 (
    .a(command_cmdtype), .b({8{1'b0}}), .gt(command_unsuported_sel), .eq(command_reg_sel));  // open: lt
  and and_28 (command_reg_exec, command_exec, command_reg_sel);
  Comparator #(.Bits(16)) comparator_18 (.a(command_reg_regno), .b(16'h1000), .lt(comparator_18_lt));  // open: gt, eq
  Comparator #(.Bits(16)) comparator_19 (.a(command_reg_regno), .b(16'h101f), .gt(comparator_19_gt));  // open: eq, lt
  Add #(.Bits(30)) add_1 (.a(ID_pc), .b({30{1'b0}}), .c_i(1'b1), .s(add_1_s));  // open: c_o
  Multiplexer #(.Bits(32)) multiplexer_15 (
    .sel(and_27_out), .in_0(command_persistent_q), .in_1(dmi_wdata),
    .out({command_cmdtype, multiplexer_15_out[23], command_reg_aarsize, command_reg_aarpostincrement, command_reg_postexec, command_reg_transfer, command_reg_write, command_reg_regno}));
  or or_12 (or_12_out, command_wen, autoexec);
  or or_13 (command_reg_regnoinvalid, comparator_18_lt, comparator_19_gt);
  Multiplexer #(.Selector_Bits(2), .Bits(32)) multiplexer_16 (
    .sel(rv5_control_1_wb_sel), .in_0(alu_out), .in_1({add_1_s, 2'b00}), .in_2(rv5_memory_1_p13),
    .in_3(csr_out), .out(d_rdin));
  and and_29 (command_exec, or_12_out, nor_2_out);
  not not_9 (not_9_out, command_reg_regnoinvalid);
  and and_30 (command_reg_arg0wen, not_10_out, command_reg_validtransferex);
  not not_10 (not_10_out, command_reg_write);
  and and_31 (command_reg_regwen, command_reg_write, command_reg_validtransferex);
  Sub #(.Bits(16)) sub_1 (
    .a(command_reg_regno), .b(16'h1000), .c_i(1'b0), .s({sub_1_s, command_reg_gprno}));  // open: c_o
  and and_32 (command_reg_jumpprogbuf, command_reg_postexec, command_reg_exec);
  and and_33 (command_reg_validtransferex, command_reg_exec, command_reg_transfer, not_9_out);
  Register #(.Bits(32)) u_abstractauto_persistent (
    .D(dmi_wdata), .C(clock), .en(abstractauto_wen),
    .Q({abstractauto_autoexecprogbuf, abstractauto_persistent, abstractauto_autoexecdata}));
  D_FF d_ff_7 (.D(command_exec), .C(clock), .Q(d_ff_7_q));  // open: nQ
  and and_34 (and_34_out, command_exec, command_reg_transfer);
  or or_14 (or_14_out, command_exec, d_ff_7_q);
  Comparator #(.Bits(32)) comparator_20 (.a(dm_wdata), .b({32{1'b0}}), .eq(comparator_20_eq));  // open: gt, lt
  not not_11 (not_11_out, comparator_20_eq);
  not not_12 (not_12_out, and_34_out);
  Comparator #(.Bits(32)) comparator_21 (.a(dmi_memaddr), .b(32'hffc), .eq(comparator_21_eq));  // open: gt, lt
  Comparator #(.Bits(32)) comparator_22 (.a(out_dm), .b({32{1'b0}}), .eq(comparator_22_eq));  // open: gt, lt
  Comparator #(.Bits(16)) comparator_23 (.a(command_reg_regno), .b(16'h1008), .eq(comparator_23_eq));  // open: gt, lt
  not not_13 (not_13_out, comparator_22_eq);
  Comparator #(.Bits(32)) comparator_24 (.a(addr_dm), .b(32'h1024), .eq(comparator_24_eq));  // open: gt, lt
  // And and_35 has open pins: In_1=not_11_out, In_2=dm_wen, In_3=not_12_out, In_4=comparator_21_eq, out=open
  // And and_36 has open pins: In_1=comparator_21_eq, In_2=not_13_out, out=open
  Comparator #(.Bits(32)) comparator_25 (
    .a({abstractauto_autoexecprogbuf, 4'b0000, abstractauto_autoexecdata}), .b({32{1'b0}}),
    .eq(comparator_25_eq));  // open: gt, lt
  and and_37 (and_37_out, comparator_23_eq, command_reg_write, 1'b1, command_reg_transfer, or_14_out);
  not not_14 (not_14_out, comparator_25_eq);
  // And and_38 has open pins: In_1=comparator_24_eq, In_2=dm_wen, In_3=dmi_wdata[2], out=open
  RS_FF_AS rs_ff_as_1 (.S(autoexec), .R(1'b0), .Q(rs_ff_as_1_q));  // open: nQ
  D_FF d_ff_8 (.D(in_1), .C(clock), .Q(d_ff_8_q));  // open: nQ
  Comparator #(.Bits(3)) comparator_26 (.a(abstractcs_cmderr), .b(3'b111));  // open: gt, eq, lt
  not not_15 (not_15_out, d_ff_8_q);
  and and_39 (and_39_out, not_15_out, in_1);
  Multiplexer multiplexer_17 (.sel(in_1), .in_0(1'b0), .in_1(1'b0), .out(multiplexer_17_out));
  or or_15 (or_15_out, 1'b0, and_39_out);
  Register register_3 (.D(multiplexer_17_out), .C(clock), .en(or_15_out), .Q(register_3_q));
  or or_16 (or_16_out, 1'b0, register_3_q);
  Multiplexer multiplexer_18 (.sel(or_17_out), .in_0(in_4), .in_1(in_4));  // open: out
  or or_17 (or_17_out, in_5, stopcond);
  and and_40 (stopcond, or_16_out, in_2);

  // Other names for the same wires on the sheet: pc[31:2] = ID_pc;
  //   abstractauto_persistent (some bits) = {abstractauto_autoexecprogbuf, abstractauto_autoexecdata};
  //   abstractauto_rdata (some bits) = {abstractauto_autoexecprogbuf, abstractauto_autoexecdata};
  //   abstractcs_rdata (some bits) = {abstractcs_busy, abstractcs_cmderr}; IF_alu_out[31:0] = alu_out;
  //   IF_br_cond = br_cond; clk = clock; IF_dcsr[31:0] = dcsr;
  //   dmcontrol_rdata (some bits) = {dmcontrol_haltreq, dmcontrol_hartreset, dmcontrol_ackhavereset, dmcontrol_hasel, dmcontrol_hartsel[9:0], dmcontrol_hartsel[19:10], dmcontrol_clrresethaltreq, dmcontrol_ndmreset, dmcontrol_dmactive};
  //   dmcontrol_persistent (some bits) = {dmcontrol_haltreq, dmcontrol_hartreset, dmcontrol_hasel, dmcontrol_hartsel[9:0], dmcontrol_hartsel[19:10], dmcontrol_ndmreset, dmcontrol_dmactive};
  //   dmcontrol_hartselhi[9:0] = dmcontrol_hartsel[19:10]; dmcontrol_hartsello[9:0] = dmcontrol_hartsel[9:0];
  //   dmcontrol_resumereq = dmcontrol_rdata[30]; dmcontrol_setresethaltreq = dmcontrol_rdata[3];
  //   dmstatus_anynonexistent = dmstatus_allnonexistent;
  //   dmstatus_rdata (some bits) = {{2{dmstatus_allresumeack}}, {2{dmstatus_allnonexistent}}, {2{dmstatus_allrunning}}, {2{dmstatus_allhalted}}};
  //   dmstatus_anyresumeack = dmstatus_allresumeack; dmstatus_anyrunning = dmstatus_allrunning; IF_dpc[31:0] = dpc;
  //   IF_dret_sel = dret_sel; IF_ebreak_sel = ebreak_sel; IF_ecall_sel = ecall_sel; in_progbuf = abstractcs_busy;
  //   inst_out (some bits) = {d_rs1, d_rd}; rs1[4:0] = d_rs1; rs2[4:0] = inst_out[24:20];
  //   system_imm[11:0] = inst_out[31:20]; dmstatus_anyhalted = dmstatus_allhalted; is_debug = dmstatus_allhalted;
  //   jalr_sel = IF_jalr_sel; mepc[31:0] = IF_mepc; mret_sel = IF_mret_sel; mtvec[31:0] = IF_mtvec;
  //   pc_jumprel[29:0] = IF_pc_jumprel; ID_wb[31:0] = d_rdin; wb[31:0] = d_rdin

  // Notes on the sheet:
  //   in_2: default 1
  //   clock: Hz: 2147483647
  //   Debug module control:
  //   GDB & TAP
  //   This is where the GDB server component and JTAG TAP live. We just plug them
  //   into each other, decode what the TAP wants us to do, and provide it with output
  //   from the circuit.
  //   Debug module registers:
  //   dmcontrol
  //   Additional debug module logic:
  //   halting
  //   We should halt if we're being asked to via dmcontrol or if we've just completed
  //   a single-step:
  //   We store any fields that need to be
  //   persistent in a register:
  //   Every RW field can be directly
  //   extracted for use from the
  //   persistent register:
  //   W1 fields should only be high
  //   for the clock cycle that they're written:
  //   Debug park loop > dret
  //   (We can get away with a hardcoded
  //   number of clock cycles for single-step.)
  //   dret > curr. instr
  //   It's useful to have each field separate
  //   for implementing their functionality,
  //   but let's also pack them up
  //   so that the debugger can read them:
  //   (And for convenience, let's 
  //   also expose this:)
  //   curr. instr > next instr
  //   We know our CPU handles halts in a
  //   single clock cycle, so to avoid complication
  //   we won't hold this signal high.
  //   sbcs
  //   We don't support system bus
  //   access, so we can treat this entire
  //   register as effectively read-only:
  //   contents of dmi_rdata_lut (hex, n*v repeats v):
  //   4*0,1,11*0,2,3,4,0,0,0,5,0,7,7*0,8*1,16*0,6
  //   contents of dmi_wen_lut (hex, n*v repeats v):
  //   16*0,1,5*0,2,3,5,31*0,4
  //   contents of dmi_memaddr_lut (hex, n*v repeats v):
  //   4*0,ffc,27*0,1004,1008,100c,1010,1014,1018,101c,1020
  //   autoexec
  //   We just check if we're accessing any data/progbuf words
  //   that we're supposed to autoexec on access of:
  //   TODO: Simplify
  //   dmstatus
  //   Every field in mstatus is read-only.
  //   (Pretty useful)
  //   Determine each field's value:
  //   Transaction signals
  //   We are done working if we're not
  //   in progbuf and dmi-req didn't just go high:
  //   We should raise dmi-ack if we are done and
  //   lower it if we need to lower it:
  //   Specifically, we should lower dmi-ack when
  //   dmi-req is lowered by the TAP in acknowledgement
  //   of our acknowledgement:
  //   Pack them up so the debugger
  //   can read them:
  //   memory access
  //   If the debug module is accessing RAM,
  //   it is either because one of the dmi
  //   registers is memory-mapped, or 
  //   we are executing a command that
  //   requires us to do so.
  //   RISC-V CPU:
  //   IF: Instruction fetch
  //   abstractcs
  //   cpu "hooks"
  //   Determine each field's value:
  //   (especially cmderr...)
  //   Sometimes we want to read or write
  //   a register:
  //   For now, address range check is
  //   the most robust way to know if
  //   we're in debug mode.
  //   Might change so debug ROM length
  //   is variable, but for now I KNOW this
  //   works.
  //   In a harvard-style CPU, there would
  //   be actual instruction memory here.
  //   Instead, we have a tunnel to our
  //   memory block and a tunnel back.
  //   We should never do an instruction's
  //   memory write while jumping for haltreq:
  //   (We process the instruction when we get
  //   back. We don't want duplicate execution!)
  //   ID: Instruction decode/register file read
  //   debug module stuff - ignore
  //   (unless curious)
  //   EX: Execute/address calculation
  //   hartinfo
  //   MEM: Memory access
  //   command
  //   This is a write-only register. 
  //   We choose to process it entirely on the same cycle it is written.
  //   I should mention that we only implement the access register
  //   command. This is because it contains functionality for arbitrary
  //   code execution, which allows us to do everything else.
  //   Handle persistence and extract all fields:
  //   Figure out if we should be executing
  //   the command:
  //   Split out cmdtype to selectors:
  //   Determine if we need to execute a register access
  //   command:
  //   Figure out if regno is invalid:
  //   WB: Write back
  //   Determine if a valid transfer is to be executed:
  //   Will we end up reading a register?
  //   Let's see:
  //   What about writing?
  //   If we end up reading or writing a
  //   register, we'll need its number in
  //   the standard format:
  //   And finally figure out if we need to
  //   jump to the progbuf:
  //   abstractauto
  //   This is an optional register, but OpenOCD
  //   is bugged and requires it. (riscv-collab/riscv-openocd/issues/587)
  //   Store for persistence:
  //   Extract the fields:
  //   Debug stuff
  //   Pack up:
endmodule
